// Logisim project ex5.circ as structural Verilog: 5 circuits, main circuit rotr
module rotr (
  input  [15:0] A,
  input  [3:0] B,
  output [15:0] out_3,
  output [15:0] Out1
);

  wire [15:0] rot1_1_out_3, rot2_1_out_3, rot4_1_out_3;

  rot1 rot1_1 (.In1(A), .sig(B[0]), .out_3(rot1_1_out_3));
  rot2 rot2_1 (.In2(rot1_1_out_3), .sig(B[1]), .out_3(rot2_1_out_3));
  rot4 rot4_1 (.In4(rot2_1_out_3), .sig(B[2]), .out_3(rot4_1_out_3));
  rot8 rot8_1 (.In8(rot4_1_out_3), .sig(B[3]), .out_3(out_3));

  // Notes on the sheet:
  //   PUT CIRCUITRY HERE
endmodule

module rot8 (
  input  [15:0] In8,
  input  sig,
  output [15:0] out_3
);

  Multiplexer #(.width(16), .enable("false")) multiplexer_1 (
    .in0(In8), .in1({In8[7:0], In8[15:8]}), .out(out_3), .sel(sig));

  // Other names for the same wires on the sheet: arm0[7:0] = In8[15:8]; arm1[7:0] = In8[7:0]

  // Notes on the sheet:
  //   PUT CIRCUITRY HERE
endmodule

module rot4 (
  input  [15:0] In4,
  input  sig,
  output [15:0] out_3
);

  Multiplexer #(.width(16), .enable("false")) multiplexer_1 (
    .in0(In4), .in1({In4[3:0], In4[15:4]}), .out(out_3), .sel(sig));

  // Other names for the same wires on the sheet: arm0[11:0] = In4[15:4]; arm1[3:0] = In4[3:0]

  // Notes on the sheet:
  //   PUT CIRCUITRY HERE
endmodule

module rot2 (
  input  [15:0] In2,
  input  sig,
  output [15:0] out_3
);

  Multiplexer #(.width(16), .enable("false")) multiplexer_1 (
    .in0(In2), .in1({In2[1:0], In2[15:2]}), .out(out_3), .sel(sig));

  // Other names for the same wires on the sheet: arm0[13:0] = In2[15:2]; arm1[1:0] = In2[1:0]

  // Notes on the sheet:
  //   PUT CIRCUITRY HERE
endmodule

module rot1 (
  input  [15:0] In1,
  input  sig,
  output [15:0] out_3
);

  Multiplexer #(.width(16), .enable("false")) multiplexer_1 (
    .in0(In1), .in1({In1[0], In1[15:1]}), .out(out_3), .sel(sig));

  // Other names for the same wires on the sheet: arm0[14:0] = In1[15:1]; arm1 = In1[0]

  // Notes on the sheet:
  //   PUT CIRCUITRY HERE
endmodule
