// Logisim project branch_comp.circ as structural Verilog: 1 circuit, main circuit branch_comp
module branch_comp (
  input  [31:0] rs1,
  input  [31:0] rs2,
  input  BrUn,
  output BrEq,
  output BrLt
);

  wire sEq, sLt, uEq, uLt;

  Comparator #(.width(32), .mode("unsigned")) comparator_1 (.a(rs1), .b(rs2), .eq(uEq), .lt(uLt));  // open: gt
  Comparator #(.width(32)) comparator_2 (.a(rs1), .b(rs2), .eq(sEq), .lt(sLt));  // open: gt
  Multiplexer #(.enable("false")) multiplexer_1 (.in0(sEq), .in1(uEq), .out(BrEq), .sel(BrUn));
  Multiplexer #(.enable("false")) multiplexer_2 (.in0(sLt), .in1(uLt), .out(BrLt), .sel(BrUn));

  // Notes on the sheet:
  //   INPUTS to your circuit
  //   DON'T CHANGE THE LOCATIONS OF THE INPUTS AND OUTPUTS!
  //   OUTPUT from your circuit
endmodule
