// Logisim project control_logic.circ as structural Verilog: 1 circuit, main circuit control_logic
module control_logic (
  input  [31:0] inst,
  input  BrEq,
  input  BrLt,
  output PCSel,
  output RegWEn,
  output [2:0] ImmSel,
  output BrUn,
  output ASel,
  output BSel,
  output [3:0] ALUSel,
  output MemRW,
  output [1:0] WBSel
);

  wire and_7_out, and_8_out, and_9_out, and_10_out, and_11_out, and_12_out, and_13_out, and_27_out,
       and_28_out, and_29_out, and_30_out, and_31_out, and_32_out, and_33_out, and_43_out, and_44_out,
       and_45_out, and_46_out, and_47_out, and_48_out, funct3_0, funct3_1, funct3_2, funct3_3, funct3_4,
       funct3_5, funct3_6, funct3_7, funct7_00, funct7_01, funct7_20, not_2_out, not_3_out, not_4_out, op03,
       op6f, op13, op17, op33, op37, op63, op67, or_1_out, or_2_out, or_4_out, or_9_out, or_11_out,
       or_14_out, PCSel_Br, PCSel_Br_0, PCSel_Br_1, PCSel_Br_4, PCSel_Br_5, PCSel_Br_6, PCSel_Br_7, PCSel_j;
  wire [1:0] bit_extender_7_out, bit_extender_8_out, WBSel_1, WBSel_2;
  wire [2:0] and_1_out, and_2_out, and_3_out, and_4_out, and_5_out, bit_extender_1_out, bit_extender_2_out,
       bit_extender_3_out, bit_extender_4_out, bit_extender_5_out;
  wire [3:0] ALUSel_1, ALUSel_1_i, ALUSel_2, ALUSel_2_i, ALUSel_3, ALUSel_3_i, ALUSel_4, ALUSel_4_i,
       ALUSel_5, ALUSel_5_i, ALUSel_6, ALUSel_6_i, ALUSel_7, ALUSel_7_i, ALUSel_8, ALUSel_9, ALUSel_a,
       ALUSel_b, ALUSel_c, ALUSel_e, ALUSel_I, ALUSel_lui, ALUSel_R, bit_extender_6_out, bit_extender_9_out,
       bit_extender_10_out, bit_extender_11_out, bit_extender_12_out, bit_extender_13_out,
       bit_extender_14_out, bit_extender_15_out, bit_extender_16_out, bit_extender_17_out,
       bit_extender_18_out, bit_extender_19_out, bit_extender_20_out, bit_extender_21_out,
       bit_extender_22_out, bit_extender_23_out, bit_extender_24_out, bit_extender_25_out,
       bit_extender_26_out, bit_extender_27_out, bit_extender_28_out;

  Comparator #(.width(7), .mode("unsigned")) comparator_1 (.a(7'b0110011), .b(inst[6:0]), .eq(op33));  // open: gt, lt
  Comparator #(.width(7), .mode("unsigned")) comparator_2 (.a(7'b0000011), .b(inst[6:0]), .eq(op03));  // open: gt, lt
  Comparator #(.width(7), .mode("unsigned")) comparator_3 (.a(7'b0010011), .b(inst[6:0]), .eq(op13));  // open: gt, lt
  Comparator #(.width(7), .mode("unsigned")) comparator_4 (.a(7'b0100011), .b(inst[6:0]), .eq(MemRW));  // open: gt, lt
  Comparator #(.width(7), .mode("unsigned")) comparator_5 (.a(7'b1100011), .b(inst[6:0]), .eq(op63));  // open: gt, lt
  or or_1 (or_1_out, op03, op13);
  or or_2 (or_2_out, op17, op37);
  assign ALUSel = ALUSel_R | ALUSel_lui | ALUSel_I;  // OR_Gate or_3, 4 bits wide
  or or_4 (or_4_out, or_1_out, op67);
  assign bit_extender_1_out = {{2{or_4_out}}, or_4_out};  // Bit_Extender bit_extender_1
  assign bit_extender_2_out = {{2{MemRW}}, MemRW};  // Bit_Extender bit_extender_2
  assign bit_extender_3_out = {{2{op63}}, op63};  // Bit_Extender bit_extender_3
  assign bit_extender_4_out = {{2{or_2_out}}, or_2_out};  // Bit_Extender bit_extender_4
  assign bit_extender_5_out = {{2{op6f}}, op6f};  // Bit_Extender bit_extender_5
  assign ALUSel_R = ALUSel_1 | ALUSel_2 | ALUSel_3 | ALUSel_4 | ALUSel_5 | ALUSel_6 | ALUSel_7 | ALUSel_8 | ALUSel_9 | ALUSel_a | ALUSel_b | ALUSel_c | ALUSel_e;  // OR_Gate or_5, 4 bits wide
  assign ALUSel_I = ALUSel_1_i | ALUSel_2_i | ALUSel_3_i | ALUSel_4_i | ALUSel_5_i | ALUSel_6_i | ALUSel_7_i;  // OR_Gate or_6, 4 bits wide
  Comparator #(.width(7), .mode("unsigned")) comparator_6 (.a(7'b0010111), .b(inst[6:0]), .eq(op17));  // open: gt, lt
  Comparator #(.width(7), .mode("unsigned")) comparator_7 (.a(7'b0110111), .b(inst[6:0]), .eq(op37));  // open: gt, lt
  Comparator #(.width(7), .mode("unsigned")) comparator_8 (.a(7'b1101111), .b(inst[6:0]), .eq(op6f));  // open: gt, lt
  Comparator #(.width(7), .mode("unsigned")) comparator_9 (.a(7'b1100111), .b(inst[6:0]), .eq(op67));  // open: gt, lt
  assign and_1_out = 3'b001 & bit_extender_1_out;  // AND_Gate and_1, 3 bits wide
  assign and_2_out = 3'b010 & bit_extender_2_out;  // AND_Gate and_2, 3 bits wide
  assign and_3_out = 3'b011 & bit_extender_3_out;  // AND_Gate and_3, 3 bits wide
  assign and_4_out = 3'b100 & bit_extender_4_out;  // AND_Gate and_4, 3 bits wide
  assign and_5_out = 3'b101 & bit_extender_5_out;  // AND_Gate and_5, 3 bits wide
  or or_7 (RegWEn, op33, op03, op13, op17, op37, op6f, op67);
  assign ImmSel = and_1_out | and_2_out | and_3_out | and_4_out | and_5_out;  // OR_Gate or_8, 3 bits wide
  assign ALUSel_lui = 4'b1101 & bit_extender_6_out;  // AND_Gate and_6, 4 bits wide
  assign bit_extender_6_out = {{3{op37}}, op37};  // Bit_Extender bit_extender_6
  not not_1 (BSel, op33);
  not not_2 (not_2_out, BrEq);
  not not_3 (not_3_out, BrLt);
  Comparator #(.width(3), .mode("unsigned")) comparator_10 (
    .a(3'b000), .b(inst[14:12]), .eq(funct3_0));  // open: gt, lt
  Comparator #(.width(3), .mode("unsigned")) comparator_11 (
    .a(3'b001), .b(inst[14:12]), .eq(funct3_1));  // open: gt, lt
  Comparator #(.width(3), .mode("unsigned")) comparator_12 (
    .a(3'b010), .b(inst[14:12]), .eq(funct3_2));  // open: gt, lt
  Comparator #(.width(3), .mode("unsigned")) comparator_13 (
    .a(3'b011), .b(inst[14:12]), .eq(funct3_3));  // open: gt, lt
  Comparator #(.width(3), .mode("unsigned")) comparator_14 (
    .a(3'b100), .b(inst[14:12]), .eq(funct3_4));  // open: gt, lt
  Comparator #(.width(3), .mode("unsigned")) comparator_15 (
    .a(3'b101), .b(inst[14:12]), .eq(funct3_5));  // open: gt, lt
  Comparator #(.width(3), .mode("unsigned")) comparator_16 (
    .a(3'b110), .b(inst[14:12]), .eq(funct3_6));  // open: gt, lt
  Comparator #(.width(3), .mode("unsigned")) comparator_17 (
    .a(3'b111), .b(inst[14:12]), .eq(funct3_7));  // open: gt, lt
  Comparator #(.width(7), .mode("unsigned")) comparator_18 (
    .a({7{1'b0}}), .b(inst[31:25]), .eq(funct7_00));  // open: gt, lt
  Comparator #(.width(7), .mode("unsigned")) comparator_19 (
    .a(7'b0000001), .b(inst[31:25]), .eq(funct7_01));  // open: gt, lt
  Comparator #(.width(7), .mode("unsigned")) comparator_20 (
    .a(7'b0100000), .b(inst[31:25]), .eq(funct7_20));  // open: gt, lt
  and and_7 (and_7_out, op33, funct3_7, funct7_00);
  and and_8 (and_8_out, op33, funct3_6, funct7_00);
  and and_9 (and_9_out, op33, funct3_4, funct7_00);
  and and_10 (and_10_out, op33, funct3_5, funct7_00);
  and and_11 (and_11_out, op33, funct3_5, funct7_20);
  and and_12 (and_12_out, op33, funct3_1, funct7_00);
  and and_13 (and_13_out, op33, funct3_2, funct7_00);
  assign bit_extender_7_out = {{1{op03}}, op03};  // Bit_Extender bit_extender_7
  assign bit_extender_8_out = {{1{or_9_out}}, or_9_out};  // Bit_Extender bit_extender_8
  or or_9 (or_9_out, op6f, op67);
  and and_14 (PCSel_Br_0, BrEq, funct3_0);
  and and_15 (PCSel_Br_1, not_2_out, funct3_1);
  and and_16 (PCSel_Br_4, BrLt, funct3_4);
  and and_17 (PCSel_Br_5, not_3_out, funct3_5);
  assign bit_extender_9_out = {{3{and_7_out}}, and_7_out};  // Bit_Extender bit_extender_9
  assign bit_extender_10_out = {{3{and_8_out}}, and_8_out};  // Bit_Extender bit_extender_10
  assign bit_extender_11_out = {{3{and_9_out}}, and_9_out};  // Bit_Extender bit_extender_11
  assign bit_extender_12_out = {{3{and_10_out}}, and_10_out};  // Bit_Extender bit_extender_12
  assign bit_extender_13_out = {{3{and_11_out}}, and_11_out};  // Bit_Extender bit_extender_13
  assign bit_extender_14_out = {{3{and_12_out}}, and_12_out};  // Bit_Extender bit_extender_14
  assign bit_extender_15_out = {{3{and_13_out}}, and_13_out};  // Bit_Extender bit_extender_15
  assign WBSel_1 = 2'b01 & bit_extender_7_out;  // AND_Gate and_18, 2 bits wide
  assign WBSel_2 = 2'b10 & bit_extender_8_out;  // AND_Gate and_19, 2 bits wide
  assign WBSel = WBSel_1 | WBSel_2;  // OR_Gate or_10, 2 bits wide
  assign ALUSel_1 = 4'b0001 & bit_extender_9_out;  // AND_Gate and_20, 4 bits wide
  assign ALUSel_2 = 4'b0010 & bit_extender_10_out;  // AND_Gate and_21, 4 bits wide
  assign ALUSel_3 = 4'b0011 & bit_extender_11_out;  // AND_Gate and_22, 4 bits wide
  assign ALUSel_4 = 4'b0100 & bit_extender_12_out;  // AND_Gate and_23, 4 bits wide
  assign ALUSel_5 = 4'b0101 & bit_extender_13_out;  // AND_Gate and_24, 4 bits wide
  assign ALUSel_6 = 4'b0110 & bit_extender_14_out;  // AND_Gate and_25, 4 bits wide
  assign ALUSel_7 = 4'b0111 & bit_extender_15_out;  // AND_Gate and_26, 4 bits wide
  and and_27 (and_27_out, op13, funct3_1, funct7_00);
  and and_28 (and_28_out, op13, funct3_2);
  and and_29 (and_29_out, op13, funct3_4);
  and and_30 (and_30_out, op13, funct3_5, funct7_00);
  and and_31 (and_31_out, op13, funct3_5, funct7_20);
  and and_32 (and_32_out, op13, funct3_6);
  and and_33 (and_33_out, op13, funct3_7);
  not not_4 (not_4_out, BrLt);
  assign bit_extender_16_out = {{3{and_27_out}}, and_27_out};  // Bit_Extender bit_extender_16
  assign bit_extender_17_out = {{3{and_28_out}}, and_28_out};  // Bit_Extender bit_extender_17
  assign bit_extender_18_out = {{3{and_29_out}}, and_29_out};  // Bit_Extender bit_extender_18
  assign bit_extender_19_out = {{3{and_30_out}}, and_30_out};  // Bit_Extender bit_extender_19
  assign bit_extender_20_out = {{3{and_31_out}}, and_31_out};  // Bit_Extender bit_extender_20
  assign bit_extender_21_out = {{3{and_32_out}}, and_32_out};  // Bit_Extender bit_extender_21
  assign bit_extender_22_out = {{3{and_33_out}}, and_33_out};  // Bit_Extender bit_extender_22
  and and_34 (PCSel_Br_6, BrLt, funct3_6);
  and and_35 (PCSel_Br_7, not_4_out, funct3_7);
  assign ALUSel_6_i = 4'b0110 & bit_extender_16_out;  // AND_Gate and_36, 4 bits wide
  assign ALUSel_7_i = 4'b0111 & bit_extender_17_out;  // AND_Gate and_37, 4 bits wide
  assign ALUSel_3_i = 4'b0011 & bit_extender_18_out;  // AND_Gate and_38, 4 bits wide
  assign ALUSel_4_i = 4'b0100 & bit_extender_19_out;  // AND_Gate and_39, 4 bits wide
  assign ALUSel_5_i = 4'b0101 & bit_extender_20_out;  // AND_Gate and_40, 4 bits wide
  assign ALUSel_2_i = 4'b0010 & bit_extender_21_out;  // AND_Gate and_41, 4 bits wide
  assign ALUSel_1_i = 4'b0001 & bit_extender_22_out;  // AND_Gate and_42, 4 bits wide
  and and_43 (and_43_out, op33, funct3_5, funct7_01);
  and and_44 (and_44_out, op33, funct3_7, funct7_01);
  and and_45 (and_45_out, op33, funct3_0, funct7_01);
  and and_46 (and_46_out, op33, funct3_3, funct7_01);
  and and_47 (and_47_out, op33, funct3_0, funct7_20);
  and and_48 (and_48_out, op33, funct3_1, funct7_01);
  or or_11 (or_11_out, funct3_6, funct3_7);
  or or_12 (ASel, op63, op17, op6f);
  or or_13 (PCSel_j, op6f, op67);
  or or_14 (or_14_out, PCSel_Br_0, PCSel_Br_1, PCSel_Br_4, PCSel_Br_5, PCSel_Br_6, PCSel_Br_7);
  and and_49 (PCSel_Br, or_14_out, op63);
  assign bit_extender_23_out = {{3{and_43_out}}, and_43_out};  // Bit_Extender bit_extender_23
  assign bit_extender_24_out = {{3{and_44_out}}, and_44_out};  // Bit_Extender bit_extender_24
  assign bit_extender_25_out = {{3{and_45_out}}, and_45_out};  // Bit_Extender bit_extender_25
  assign bit_extender_26_out = {{3{and_46_out}}, and_46_out};  // Bit_Extender bit_extender_26
  assign bit_extender_27_out = {{3{and_47_out}}, and_47_out};  // Bit_Extender bit_extender_27
  assign bit_extender_28_out = {{3{and_48_out}}, and_48_out};  // Bit_Extender bit_extender_28
  and and_50 (BrUn, op63, or_11_out);
  assign ALUSel_8 = 4'b1000 & bit_extender_23_out;  // AND_Gate and_51, 4 bits wide
  assign ALUSel_9 = 4'b1001 & bit_extender_24_out;  // AND_Gate and_52, 4 bits wide
  assign ALUSel_a = 4'b1010 & bit_extender_25_out;  // AND_Gate and_53, 4 bits wide
  assign ALUSel_b = 4'b1011 & bit_extender_26_out;  // AND_Gate and_54, 4 bits wide
  assign ALUSel_c = 4'b1100 & bit_extender_27_out;  // AND_Gate and_55, 4 bits wide
  assign ALUSel_e = 4'b1110 & bit_extender_28_out;  // AND_Gate and_56, 4 bits wide
  or or_15 (PCSel, PCSel_j, PCSel_Br);

  // Other names for the same wires on the sheet: opcode[6:0] = inst[6:0]; funct3[2:0] = inst[14:12];
  //   funct7[6:0] = inst[31:25]; op23 = MemRW

  // Notes on the sheet:
  //   INPUTS to your circuit
  //   DON'T CHANGE THE LOCATIONS OF THE INPUTS AND OUTPUTS!
  //   OUTPUT from your circuit
endmodule
