// Logisim project cpu.circ as structural Verilog: 1 circuit, main circuit main
module main (
  input  [31:0] INSTRUCTION,
  input  in_2,
  output [31:0] PROGRAM_COUNTER,
  output [31:0] ra,
  output [31:0] sp,
  output [31:0] t0,
  output [31:0] t1,
  output [31:0] t2,
  output [31:0] s0,
  output [31:0] s1,
  output [31:0] a0
);

  wire ASel_1, branch_comp_1_breq, branch_comp_1_brlt, BSel_1, comparator_1_eq, comparator_2_gt,
       comparator_3_eq, comparator_4_gt, control_logic_1_brun, data_hazard1, data_hazard2, MemRW_1, PCSel_1,
       RegWEn_1;
  wire [1:0] WBSel_1;
  wire [2:0] ImmSel_1;
  wire [3:0] ALUSel_1;
  wire [4:0] Addrd, Addrd_1, Addrs1, Addrs1_1, Addrs2, Addrs2_1;
  wire [31:0] adder_1_out, adder_2_out, ALUres_1, bit_extender_1_out, bit_extender_2_out, DataR_1, DMEM_p5,
       imm_1, inst, inst_1, multiplexer_1_out, multiplexer_3_out, multiplexer_4_out, multiplexer_5_out,
       multiplexer_6_out, PROGRAM_COUNTER_1, rs1, rs1_1, rs2, rs2_1, wb_1;

  control_logic control_logic_1 (
    .BSel(BSel_1), .ASel(ASel_1), .BrUn(control_logic_1_brun), .ImmSel(ImmSel_1), .RegWEn(RegWEn_1),
    .PCSel(PCSel_1), .BrLt(branch_comp_1_brlt), .BrEq(branch_comp_1_breq),
    .inst({inst_1[31:25], Addrs2_1, Addrs1_1, inst_1[14:12], Addrd_1, inst_1[6:0]}), .ALUSel(ALUSel_1),
    .MemRW(MemRW_1), .WBSel(WBSel_1));
  Adder #(.width(32)) adder_1 (.a(PROGRAM_COUNTER), .b(32'h4), .out(adder_1_out));  // open: cin, cout
  Register #(.width(32)) register_1 (.D(PROGRAM_COUNTER), .clk(in_2), .Q(PROGRAM_COUNTER_1));  // open: en, clr
  Register #(.width(32)) register_2 (
    .D({inst[31:25], Addrs2, Addrs1, inst[14:12], Addrd, inst[6:0]}), .clk(in_2),
    .Q({inst_1[31:25], Addrs2_1, Addrs1_1, inst_1[14:12], Addrd_1, inst_1[6:0]}));  // open: en, clr
  Multiplexer #(.width(32), .enable("false")) multiplexer_1 (
    .in0(adder_1_out), .in1(ALUres_1), .out(multiplexer_1_out), .sel(PCSel_1));
  Register #(.width(32)) PC (.D(multiplexer_1_out), .clk(in_2), .Q(PROGRAM_COUNTER));  // open: en, clr
  imm_gen imm_gen_1 (
    .ImmSel(ImmSel_1), .inst({inst_1[31:25], Addrs2_1, Addrs1_1, inst_1[14:12], Addrd_1, inst_1[6:0]}),
    .imm(imm_1));
  Multiplexer #(.width(32), .enable("false")) multiplexer_2 (
    .in0(INSTRUCTION), .in1({32{1'b0}}), .out({inst[31:25], Addrs2, Addrs1, inst[14:12], Addrd, inst[6:0]}),
    .sel(PCSel_1));
  Register #(.width(32)) register_3 (.D(multiplexer_3_out), .clk(in_2), .Q(rs1_1));  // open: en, clr
  Multiplexer #(.width(32), .enable("false")) multiplexer_3 (
    .in0(rs1), .in1(wb_1), .out(multiplexer_3_out), .sel(data_hazard1));
  Register #(.width(32)) register_4 (.D(multiplexer_4_out), .clk(in_2), .Q(rs2_1));  // open: en, clr
  Multiplexer #(.width(32), .enable("false")) multiplexer_4 (
    .in0(rs2), .in1(wb_1), .out(multiplexer_4_out), .sel(data_hazard2));
  branch_comp branch_comp_1 (
    .BrEq(branch_comp_1_breq), .BrUn(control_logic_1_brun), .rs1(rs1_1), .BrLt(branch_comp_1_brlt),
    .rs2(rs2_1));
  regfile_main RegFile (
    .rs2(Addrs2), .rd(Addrd_1), .Read_Data_1(rs1), .Read_Data_2(rs2), .ra(ra), .sp(sp), .t0(t0), .t1(t1),
    .t2(t2), .s0(s0), .s1(s1), .a0(a0), .rs1(Addrs1), .Write_Data(wb_1), .RegWEn(RegWEn_1), .clk(in_2));
  Comparator #(.width(5), .mode("unsigned")) comparator_1 (
    .a(Addrd_1), .b(Addrs1), .eq(comparator_1_eq));  // open: gt, lt
  Comparator #(.width(5), .mode("unsigned")) comparator_2 (
    .a(Addrd_1), .b({5{1'b0}}), .gt(comparator_2_gt));  // open: eq, lt
  Comparator #(.width(5), .mode("unsigned")) comparator_3 (
    .a(Addrd_1), .b(Addrs2), .eq(comparator_3_eq));  // open: gt, lt
  Comparator #(.width(5), .mode("unsigned")) comparator_4 (
    .a(Addrd_1), .b({5{1'b0}}), .gt(comparator_4_gt));  // open: eq, lt
  and and_1 (data_hazard1, comparator_1_eq, RegWEn_1, comparator_2_gt);
  and and_2 (data_hazard2, comparator_3_eq, RegWEn_1, comparator_4_gt);
  Multiplexer #(.width(32), .enable("false")) multiplexer_5 (
    .in0(rs1_1), .in1(PROGRAM_COUNTER_1), .out(multiplexer_5_out), .sel(ASel_1));
  Multiplexer #(.width(32), .enable("false")) multiplexer_6 (
    .in0(rs2_1), .in1(imm_1), .out(multiplexer_6_out), .sel(BSel_1));
  alu Arithmetic_Logic_Unit (.ALUSel(ALUSel_1), .Result(ALUres_1), .A(multiplexer_5_out), .B(multiplexer_6_out));
  // mem_main DMEM: pin names not known; wires that end beside it: ALUres_1, rs2_1, in_2, MemRW_1, DMEM_p5
  Multiplexer #(.select(2), .width(32), .enable("false")) multiplexer_7 (
    .in0(ALUres_1), .in1(DataR_1), .in2(adder_2_out), .out(wb_1), .sel(WBSel_1));  // open: in3
  Adder #(.width(32)) adder_2 (.a(PROGRAM_COUNTER_1), .b(32'h4), .out(adder_2_out));  // open: cin, cout
  assign bit_extender_1_out = {{24{DMEM_p5[7]}}, DMEM_p5[7:0]};  // Bit_Extender bit_extender_1
  assign bit_extender_2_out = {{16{DMEM_p5[15]}}, DMEM_p5[15:0]};  // Bit_Extender bit_extender_2
  Multiplexer #(.select(2), .width(32), .enable("false")) multiplexer_8 (
    .in0(bit_extender_1_out), .in1(bit_extender_2_out), .in2(DMEM_p5), .out(DataR_1), .sel(inst_1[13:12]));  // open: in3

  // Other names for the same wires on the sheet: clk = in_2; inst (some bits) = {Addrs2, Addrs1, Addrd};
  //   inst_1 (some bits) = {Addrs2_1, Addrs1_1, Addrd_1}

  // Notes on the sheet:
  //   Output
  //   IMEM (do **NOT** move this)
  //   Inputs
  //   It is OK to move the PC, RegFile, ALU, MEM, Branch Comp, Imm Gen, and Control Logic to wherever is most convenient for you when constructing your CPU, and to delete this text
  //   Inputs/Outputs for testing. Do **NOT** move these.
endmodule
