// Logisim project regfile.circ as structural Verilog: 1 circuit, main circuit main
module main (
  input  [4:0] rs1,
  input  [4:0] rs2,
  input  [4:0] rd,
  input  [31:0] Write_Data,
  input  RegWEn,
  input  clk,
  output [31:0] ra,
  output [31:0] sp,
  output [31:0] t0,
  output [31:0] t1,
  output [31:0] t2,
  output [31:0] s0,
  output [31:0] s1,
  output [31:0] a0,
  output [31:0] Read_Data_1,
  output [31:0] Read_Data_2
);

  wire WE1, WE2, WE3, WE4, WE5, WE6, WE7, WE8;
  wire [4:0] bit_extender_1_out, write_reg1;
  wire [31:0] x0;

  Decoder #(.select(4)) decoder_1 (
    .out1(WE1), .out2(WE2), .out5(WE3), .out6(WE4), .out7(WE5), .out8(WE6), .out9(WE7), .out10(WE8),
    .sel(write_reg1[3:0]));  // open: out0, out3, out4, out11, out12, out13, out14, out15, en
  assign bit_extender_1_out = {{4{RegWEn}}, RegWEn};  // Bit_Extender bit_extender_1
  assign write_reg1 = bit_extender_1_out & rd;  // AND_Gate and_1, 5 bits wide
  Register #(.width(32)) register_1 (.D(Write_Data), .en(WE1), .clk(clk), .Q(ra));  // open: clr
  Register #(.width(32)) register_2 (.D(Write_Data), .en(WE4), .clk(clk), .Q(t1));  // open: clr
  Register #(.width(32)) register_3 (.D(Write_Data), .en(WE7), .clk(clk), .Q(s1));  // open: clr
  Multiplexer #(.select(5), .width(32), .enable("false")) multiplexer_1 (
    .in0(x0), .in1(ra), .in2(sp), .in5(t0), .in6(t1), .in7(t2), .in8(s0), .in9(s1), .in10(a0),
    .out(Read_Data_1), .sel(rs1));  // open: in3, in4, in11, in12, in13, in14, in15, in16, in17, in18, in19, in20, in21, in22, in23, in24, in25, in26, in27, in28, in29, in30, in31
  Register #(.width(32)) register_4 (.D(Write_Data), .en(WE2), .clk(clk), .Q(sp));  // open: clr
  Register #(.width(32)) register_5 (.D(Write_Data), .en(WE5), .clk(clk), .Q(t2));  // open: clr
  Register #(.width(32)) register_6 (.D(Write_Data), .en(WE8), .clk(clk), .Q(a0));  // open: clr
  Register #(.width(32)) register_7 (.D(Write_Data), .en(WE3), .clk(clk), .Q(t0));  // open: clr
  Register #(.width(32)) register_8 (.D(Write_Data), .en(WE6), .clk(clk), .Q(s0));  // open: clr
  Register #(.width(32)) register_9 (.D(Write_Data), .en(1'b0), .clk(clk), .Q(x0));  // open: clr
  Multiplexer #(.select(5), .width(32), .enable("false")) multiplexer_2 (
    .in0(x0), .in1(ra), .in2(sp), .in5(t0), .in6(t1), .in7(t2), .in8(s0), .in9(s1), .in10(a0),
    .out(Read_Data_2), .sel(rs2));  // open: in3, in4, in11, in12, in13, in14, in15, in16, in17, in18, in19, in20, in21, in22, in23, in24, in25, in26, in27, in28, in29, in30, in31

  // Other names for the same wires on the sheet: read_data1[31:0] = Read_Data_1; read_data2[31:0] = Read_Data_2;
  //   read_reg1[4:0] = rs1; read_reg2[4:0] = rs2; write_en = RegWEn; write_reg[4:0] = rd

  // Notes on the sheet:
  //   INPUTS to your circuit
  //   DON'T CHANGE THE LOCATIONS OF THE INPUTS AND OUTPUTS!
  //   These are DEBUG/TEST outputs from your circuit.
  //   OUTPUTS from your circuit
endmodule
